# Fritzing sketch Hydro 1 (saved by Fritzing 0.9.9b)

parts:
  Bauteil1 = Arduino Uno (Rev3) - ICSP
  Bauteil2 = InvenSense MPU6050
  U1 = MAX6675 [package=so08]
  U2 = MAX6675 [package=so08]
  J1 = Basic Servo
  J2 = Basic Servo
  Bauteil3 = Bluetooth HC-05 Macho
  R2 = Resistor [tolerance=±5% power=0.25 resistance=2k package=THT]
  R1 = Resistor [tolerance=±5% power=0.25 resistance=1k package=THT]

nets:
  N1: Bauteil1.A4/SDA, Bauteil2.SDA
  N2: Bauteil1.A5/SCL, Bauteil2.SCL
  N3: Bauteil1.ICSP_MISO, Bauteil1.D12/MISO, Bauteil3.TXD
  N4: Bauteil1.ICSP_MOSI, Bauteil1.D11_PWM/MOSI, R1.Pin_0
  N5: Bauteil1.D8, Bauteil2.INT
  N6: Bauteil1.D9_PWM, J2.pulse
  N7: Bauteil1.D10_PWM/SS, J1.pulse
  GND: Bauteil1.GND, Bauteil2.GND, U1.VSS, U2.VSS, J1.gnd, J2.gnd, Bauteil3.GND, R2.Pin_1
  N8: Bauteil1.D2, U2.MISO
  N9: Bauteil1.D3_PWM, U2.CS
  N10: Bauteil1.D4, U2.SCK
  N11: Bauteil1.D5_PWM, U1.MISO
  N12: Bauteil1.D6_PWM, U1.CS
  N13: Bauteil1.D7, U1.SCK
  VCC: Bauteil1.5V, Bauteil2.VCC, U1.VDD, J1.vcc, J2.vcc, Bauteil3.VCC
  N14: Bauteil3.RXD, R2.Pin_0, R1.Pin_1
